# Fritzing sketch placa1.1 (saved by Fritzing 0.8.7b)
circuit board: 17.9926cm x 9.2402cm
breadboards: 2

parts:
  U2 = ESP8266 NodeMCU LoLin module
  SparkFun_74HC4051_8-Channel_Mux_Breakout1 = SparkFun-74HC4051-8-Channel-Mux-Breakout [part_number=BOB-13906]
  LED1 = LED - 5mm [color="Red (633nm)" package="5 mm [THT]"]
  LED2 = LED - 5mm [color="Red (633nm)" package="5 mm [THT]"]
  LED3 = LED - 5mm [color="Red (633nm)" package="5 mm [THT]"]
  R1 = Resistor [tolerance=±5% resistance=220 package=THT]
  R2 = Resistor [tolerance=±5% resistance=220 package=THT]
  R3 = Resistor [tolerance=±5% resistance=220 package=THT]
  S1 = Pushbutton [package=THT]
  R4 = Resistor [tolerance=±5% resistance=220 package=THT]
  TCRT1 = TCRT5000 sensor module [part_number=151608]
  TCRT2 = TCRT5000 sensor module [part_number=151608]
  Part1 = KY-015 Temperature & Humidity Sensor Module [package="Breakout board"]
  Parte1 = Adafruit BMP180

nets:
  N1: U2.D0, R1.Pin_1
  N2: U2.D1, R2.Pin_1
  N3: U2.D2, R3.Pin_1
  GND: U2.GND, U2.Vin, U2.RST, U2.EN, U2.SK, U2.S0, U2.SC, U2.S1, U2.S2, U2.S3, U2.VU, U2.A0, SparkFun_74HC4051_8-Channel_Mux_Breakout1.GND, SparkFun_74HC4051_8-Channel_Mux_Breakout1.VEE, SparkFun_74HC4051_8-Channel_Mux_Breakout1.Z, LED1.cathode, LED2.cathode, LED3.cathode, S1.leg0, R4.Pin_1, TCRT1.T+, TCRT2.T+, Parte1.GND
  N4: U2.D5, TCRT1.D-
  N5: U2.D6, TCRT2.D-
  N6: U2.D7, Part1.S
  N7: U2.D8, SparkFun_74HC4051_8-Channel_Mux_Breakout1.S2
  N8: U2.RX, SparkFun_74HC4051_8-Channel_Mux_Breakout1.S1
  N9: U2.TX, SparkFun_74HC4051_8-Channel_Mux_Breakout1.S0
  N10: SparkFun_74HC4051_8-Channel_Mux_Breakout1.Y5, Parte1.SCL
  N11: SparkFun_74HC4051_8-Channel_Mux_Breakout1.Y4, Parte1.+3V3, Parte1.SDA
  N12: SparkFun_74HC4051_8-Channel_Mux_Breakout1.VCC, TCRT1.T-, TCRT2.T-
  N13: LED1.anode, R1.Pin_0
  N14: LED2.anode, R2.Pin_0
  N15: LED3.anode, R3.Pin_0
  N16: S1.leg1, R4.Pin_0

custom parts:
  ESP8266 NodeMCU LoLin module: ESP8266 based NodeMCU
  TCRT5000 sensor module: breakout board with TCRT5000
  KY-015 Temperature & Humidity Sensor Module: KY-015 temperature and humidity sensor module, provides a low-latency serial interface to measure humidity and temperature.
  Adafruit BMP180: This precision sensor from Bosch is the best low-cost sensing solution for measuring barometric pressure and temperature. Because pressure changes with altitude you can also use it as an altimeter! The sensor is soldered onto a PCB with a 3.3V regulator, I2C level shifter and pull-up resistors on the I2C pins. The BMP180 is the next-generation of sensors from Bosch, and replaces the BMP085.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
